# Fritzing sketch lab-diagrama (saved by Fritzing 1.0.4)
breadboards: 1

parts:
  Mod1 = Raspberry Pi Pico
  KY-1 = Keyes Relay [package=THT]
  LED1 = DUO LED RG [package="5 mm [THT]"]
  R1 = Resistor [tolerance=±5% resistance=220 package="2512 [SMD]"]
  R2 = Resistor [tolerance=±5% resistance=220 package="2512 [SMD]"]
  Componente1 = Thumb Joystick
  S1 = Tilt Switch [package=THT]
  R3 = Resistor [tolerance=±5% resistance=10k package="0805 [SMD]"]
  J1 = Basic Servo

nets:
  N1: Mod1.pin_3, Mod1.pin_8, Mod1.pin_13, Mod1.pin_18, Mod1.pin_23, Mod1.pin_28, Mod1.pin_33, Mod1.pin_38, KY-1.power, R2.Pin_0, Componente1.VCC, S1.Pin_2
  N2: Mod1.pin_15, J1.pulse
  N3: Mod1.pin_16, KY-1.signal
  N4: Mod1.pin_17, R1.Pin_0
  N5: Mod1.pin_20, S1.Pin_1, R3.Pin_1
  N6: Mod1.pin_31, Componente1.VERT
  GND: Mod1.pin_34, KY-1.ground, LED1.common_cathode, Componente1.GND, R3.Pin_0, J1.gnd
  N7: Mod1.pin_39, J1.vcc
  N8: LED1.red_anode, R1.Pin_1
  N9: LED1.green_anode, R2.Pin_1

custom parts:
  Raspberry Pi Pico: Raspberry Pi Pico. Based around the RP2040 microcontroller the Pico is a low cost microcontroller device bringing Raspberry Pi quality, cost, and easy of use to the microcontroller space. Jan 2021, Split part in to two versions: tht (this one) and SMD. This one will drill holes for a .1 in header in pcb to allow plugging in the module as well as providing pads to solder the module to the top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
  Keyes Relay: The Keyes 5V relay module is suitable for SCM development, home appliance control. It uses a 5V~12V TIL control signal which can control DC / AC signal.
